// Logisim project Proj 1.circ as structural Verilog: 14 circuits, main circuit MIPS32
module MIPS32 (
  input  [31:0] FromMem
);

  wire clock_1_out, decode_1_mux1, decode_1_mux2, decode_1_sasel, decode_1_signed, decode_1_writeenable1,
       decode_1_writeenable2, execute_1_wer_out, isolate34_1_wbmux_out, isolate34_1_wer_out,
       isolator_2_3_1_immmux_out, isolator_2_3_1_signed_out, isolator_2_3_1_wbmux_out,
       isolator_2_3_1_wed_out, isolator_2_3_1_wer_out, registerfile_1_p3;
  wire [1:0] decode_1_extend;
  wire [3:0] decode_1_alu_code, isolator_2_3_1_alu_out;
  wire [4:0] isolate34_1_rd_out, isolator_2_3_1_rd_out, isolator_2_3_1_rs_out, isolator_2_3_1_rt_out,
       isolator_2_3_1_sa_out, multiplexer_1_out, registerfile_1_p4, savar_1_sa_out, split_1_rd, split_1_rs,
       split_1_rt, split_1_shamt;
  wire [5:0] split_1_func, split_1_op;
  wire [15:0] split_1_imm;
  wire [31:0] bitextend_1_imm_out, count_1_1_pc_4, execute_1_c_out, isolate12_1_instr_out,
       isolate12_1_pc_out, isolate34_1_c_out, isolate34_1_pc_out, isolator_2_3_1_a_out, isolator_2_3_1_b_out,
       isolator_2_3_1_imm_out, isolator_2_3_1_pc_out, mipsprogramrom_1_p2, multiplexer_2_out, register_1_q,
       registerfile_1_p1, registerfile_1_p7, registerfile_1_p8;

  Clock clock_1 (.out(clock_1_out));
  Count__1 count_1_1 (.PC(register_1_q), .PC_4(count_1_1_pc_4));
  Register #(.width(32)) register_1 (.D(count_1_1_pc_4), .Q(register_1_q), .clk(clock_1_out));  // open: en, clr
  // MIPSProgramROM mipsprogramrom_1: pin names not known; wires that end beside it: register_1_q, mipsprogramrom_1_p2
  Isolate12 isolate12_1 (
    .PC_in(register_1_q), .Instr_in(mipsprogramrom_1_p2), .clock(clock_1_out), .PC_out(isolate12_1_pc_out),
    .Instr_out(isolate12_1_instr_out));
  Split split_1 (
    .Instr(isolate12_1_instr_out), .rs(split_1_rs), .rt(split_1_rt), .shamt(split_1_shamt), .rd(split_1_rd),
    .Imm(split_1_imm), .Op(split_1_op), .Func(split_1_func));
  Decode decode_1 (
    .Op(split_1_op), .Func(split_1_func), .SAsel(decode_1_sasel), .ALU_code(decode_1_alu_code),
    .MUX1(decode_1_mux1), .MUX2(decode_1_mux2), .WriteEnable1(decode_1_writeenable1),
    .WriteEnable2(decode_1_writeenable2), .Signed(decode_1_signed), .Extend(decode_1_extend));
  // RegisterFile registerfile_1: pin names not known; wires that end beside it: registerfile_1_p1, clock_1_out, registerfile_1_p3, registerfile_1_p4, split_1_rs, split_1_rt, registerfile_1_p7, registerfile_1_p8
  Multiplexer #(.width(5)) multiplexer_1 (
    .in0(split_1_rd), .in1(split_1_rt), .out(multiplexer_1_out), .sel(decode_1_mux1));  // open: en
  BitExtend bitextend_1 (.Imm_In(split_1_imm), .BitEx(decode_1_extend), .Imm_Out(bitextend_1_imm_out));
  SAVar savar_1 (.Select(decode_1_sasel), .SA_in(split_1_shamt), .A_in(registerfile_1_p7), .SA_out(savar_1_sa_out));
  Isolator_2_3 isolator_2_3_1 (
    .rs_in(split_1_rs), .rt_in(split_1_rt), .PC_in(isolate12_1_pc_out), .Imm_in(bitextend_1_imm_out),
    .A_in(registerfile_1_p7), .B_in(registerfile_1_p8), .rd_in(multiplexer_1_out), .sa_in(savar_1_sa_out),
    .ALU_in(decode_1_alu_code), .ImmMux_in(decode_1_mux1), .WBMUX_in(decode_1_mux2),
    .WER_in(decode_1_writeenable1), .WED_in(decode_1_writeenable2), .Signed_in(decode_1_signed),
    .clock(clock_1_out), .rs_out(isolator_2_3_1_rs_out), .rt_out(isolator_2_3_1_rt_out),
    .PC_out(isolator_2_3_1_pc_out), .Imm_out(isolator_2_3_1_imm_out), .A_out(isolator_2_3_1_a_out),
    .B_out(isolator_2_3_1_b_out), .rd_out(isolator_2_3_1_rd_out), .sa_out(isolator_2_3_1_sa_out),
    .ALU_out(isolator_2_3_1_alu_out), .ImmMux_out(isolator_2_3_1_immmux_out),
    .WBMUX_out(isolator_2_3_1_wbmux_out), .WER_out(isolator_2_3_1_wer_out), .WED_out(isolator_2_3_1_wed_out),
    .Signed_out(isolator_2_3_1_signed_out));
  Execute execute_1 (
    .ALUcode(isolator_2_3_1_alu_out), .Out2(registerfile_1_p1), .WEin(isolator_2_3_1_wer_out),
    .Out1(isolate34_1_c_out), .SA(isolator_2_3_1_sa_out), .rd2(registerfile_1_p4), .rd1(isolate34_1_rd_out),
    .Immediate(isolator_2_3_1_imm_out), .ImmMux(isolator_2_3_1_immmux_out),
    .Signed(isolator_2_3_1_signed_out), .WER_out(execute_1_wer_out), .rt(isolator_2_3_1_rt_out),
    .rs(isolator_2_3_1_rs_out), .B(isolator_2_3_1_b_out), .A(isolator_2_3_1_a_out), .C_out(execute_1_c_out),
    .WE2(registerfile_1_p3), .WE1(isolate34_1_wer_out));
  Isolate_45 isolate_45_1 (
    .C_in(multiplexer_2_out), .PC_in(isolate34_1_pc_out), .rd_in(isolate34_1_rd_out),
    .WER_in(isolate34_1_wer_out), .clock(clock_1_out), .C_out(registerfile_1_p1), .rd_out(registerfile_1_p4),
    .WER_out(registerfile_1_p3));  // open: PC_out
  Isolate34 isolate34_1 (
    .C_in(execute_1_c_out), .PC_in(isolator_2_3_1_pc_out), .rd_in(isolator_2_3_1_rd_out),
    .WBMUX_in(isolator_2_3_1_wbmux_out), .WER_in(execute_1_wer_out), .WED_in(isolator_2_3_1_wed_out),
    .clock(clock_1_out), .C_out(isolate34_1_c_out), .PC_out(isolate34_1_pc_out), .rd_out(isolate34_1_rd_out),
    .WBMUX_out(isolate34_1_wbmux_out), .WER_out(isolate34_1_wer_out));  // open: WED_out
  Multiplexer #(.width(32), .enable("false")) multiplexer_2 (
    .in0(isolate34_1_c_out), .in1(FromMem), .out(multiplexer_2_out), .sel(isolate34_1_wbmux_out));
endmodule

module Count__1 (
  input  [31:0] PC,
  output [31:0] PC_4
);

  // Incrementer incrementer_1: pin names not known; wires that end beside it: PC[31:2], PC_4[31:2]

  assign PC_4[1:0] = PC[1:0];
endmodule

module Split (
  input  [31:0] Instr,
  output [4:0] rs,
  output [4:0] rt,
  output [4:0] shamt,
  output [4:0] rd,
  output [15:0] Imm,
  output [5:0] Op,
  output [5:0] Func
);


  assign Func = Instr[5:0];
  assign Imm = Instr[15:0];
  assign Op = Instr[31:26];
  assign rd = Instr[15:11];
  assign rs = Instr[25:21];
  assign rt = Instr[20:16];
  assign shamt = Instr[10:6];
endmodule

module Isolator_2_3 (
  input  [4:0] rs_in,
  input  [4:0] rt_in,
  input  [31:0] PC_in,
  input  [31:0] Imm_in,
  input  [31:0] A_in,
  input  [31:0] B_in,
  input  [4:0] rd_in,
  input  [4:0] sa_in,
  input  [3:0] ALU_in,
  input  ImmMux_in,
  input  WBMUX_in,
  input  WER_in,
  input  WED_in,
  input  Signed_in,
  input  clock,
  output [4:0] rs_out,
  output [4:0] rt_out,
  output [31:0] PC_out,
  output [31:0] Imm_out,
  output [31:0] A_out,
  output [31:0] B_out,
  output [4:0] rd_out,
  output [4:0] sa_out,
  output [3:0] ALU_out,
  output ImmMux_out,
  output WBMUX_out,
  output WER_out,
  output WED_out,
  output Signed_out
);

  Register #(.width(5)) rs (.D(rs_in), .Q(rs_out), .clk(clock));  // open: en, clr
  Register #(.width(5)) rt (.D(rt_in), .Q(rt_out), .clk(clock));  // open: en, clr
  Register #(.width(32)) PC (.D(PC_in), .Q(PC_out), .clk(clock));  // open: en, clr
  Register #(.width(32)) Imm (.D(Imm_in), .Q(Imm_out), .clk(clock));  // open: en, clr
  Register #(.width(32)) A (.D(A_in), .Q(A_out), .clk(clock));  // open: en, clr
  Register #(.width(32)) B (.D(B_in), .Q(B_out), .clk(clock));  // open: en, clr
  Register #(.width(5)) rd (.D(rd_in), .Q(rd_out), .clk(clock));  // open: en, clr
  Register #(.width(5)) sa (.D(sa_in), .Q(sa_out), .clk(clock));  // open: en, clr
  Register #(.width(4)) aluop (.D(ALU_in), .Q(ALU_out), .clk(clock));  // open: en, clr
  Register #(.width(1)) IE (.D(ImmMux_in), .Q(ImmMux_out), .clk(clock));  // open: en, clr
  Register #(.width(1)) WBMUX (.D(WBMUX_in), .Q(WBMUX_out), .clk(clock));  // open: en, clr
  Register #(.width(1)) WER (.D(WER_in), .Q(WER_out), .clk(clock));  // open: en, clr
  Register #(.width(1)) WED (.D(WED_in), .Q(WED_out), .clk(clock));  // open: en, clr
  Register #(.width(1)) Signed (.D(Signed_in), .Q(Signed_out), .clk(clock));  // open: en, clr
endmodule

module Isolate34 (
  input  [31:0] C_in,
  input  [31:0] PC_in,
  input  [4:0] rd_in,
  input  WBMUX_in,
  input  WER_in,
  input  WED_in,
  input  clock,
  output [31:0] C_out,
  output [31:0] PC_out,
  output [4:0] rd_out,
  output WBMUX_out,
  output WER_out,
  output WED_out
);

  Register #(.width(32)) PC (.D(C_in), .Q(C_out), .clk(clock));  // open: en, clr
  Register #(.width(32)) PC_2 (.D(PC_in), .Q(PC_out), .clk(clock));  // open: en, clr
  Register #(.width(5)) rd (.D(rd_in), .Q(rd_out), .clk(clock));  // open: en, clr
  Register #(.width(1)) WBMUX (.D(WBMUX_in), .Q(WBMUX_out), .clk(clock));  // open: en, clr
  Register #(.width(1)) WER (.D(WER_in), .Q(WER_out), .clk(clock));  // open: en, clr
  Register #(.width(1)) WED (.D(WED_in), .Q(WED_out), .clk(clock));  // open: en, clr
endmodule

module Isolate_45 (
  input  [31:0] C_in,
  input  [31:0] PC_in,
  input  [4:0] rd_in,
  input  WER_in,
  input  clock,
  output [31:0] C_out,
  output [31:0] PC_out,
  output [4:0] rd_out,
  output WER_out
);

  Register #(.width(32)) PC (.D(C_in), .Q(C_out), .clk(clock));  // open: en, clr
  Register #(.width(32)) PC_2 (.D(PC_in), .Q(PC_out), .clk(clock));  // open: en, clr
  Register #(.width(5)) rd (.D(rd_in), .Q(rd_out), .clk(clock));  // open: en, clr
  Register #(.width(1)) WER (.D(WER_in), .Q(WER_out), .clk(clock));  // open: en, clr
endmodule

module Forward (
  input  [31:0] Out2,
  input  [4:0] rd2,
  input  WE1,
  input  [4:0] rd1,
  input  [31:0] Out0,
  input  [31:0] Out1,
  input  WE2,
  input  [4:0] rs,
  output [31:0] Forwarded
);

  wire and_1_out, and_2_out, nor_1_out, nor_2_out, or_1_out;
  wire [4:0] xor_1_out, xor_2_out;
  wire [31:0] multiplexer_1_out;

  or or_1 (or_1_out, rs[0], rs[1], rs[2], rs[3], rs[4]);
  assign xor_1_out = rd1 ^ rs;  // XOR_Gate xor_1, 5 bits wide
  assign xor_2_out = rs ^ rd2;  // XOR_Gate xor_2, 5 bits wide
  nor nor_1 (nor_1_out, xor_1_out[0], xor_1_out[1], xor_1_out[2], xor_1_out[3], xor_1_out[4]);
  nor nor_2 (nor_2_out, xor_2_out[0], xor_2_out[1], xor_2_out[2], xor_2_out[3], xor_2_out[4]);
  Multiplexer #(.width(32), .enable("false")) multiplexer_1 (
    .in0(Out0), .in1(Out2), .out(multiplexer_1_out), .sel(and_1_out));
  and and_1 (and_1_out, nor_2_out, or_1_out, WE2);
  and and_2 (and_2_out, WE1, or_1_out, nor_1_out);
  Multiplexer #(.width(32), .enable("false")) multiplexer_2 (
    .in0(multiplexer_1_out), .in1(Out1), .out(Forwarded), .sel(and_2_out));
endmodule

module Isolate12 (
  input  [31:0] PC_in,
  input  [31:0] Instr_in,
  input  clock,
  output [31:0] PC_out,
  output [31:0] Instr_out
);

  Register #(.width(32)) PC (.D(PC_in), .Q(PC_out), .clk(clock));  // open: en, clr
  Register #(.width(32)) Instr (.D(Instr_in), .Q(Instr_out), .clk(clock));  // open: en, clr
endmodule

module Decode (
  input  [5:0] Op,
  input  [5:0] Func,
  output SAsel,
  output [3:0] ALU_code,
  output MUX1,
  output MUX2,
  output WriteEnable1,
  output WriteEnable2,
  output Signed,
  output [1:0] Extend
);

  wire i_j_out_1_p11, i_j_out_1_p12, i_j_out_1_p13, i_j_out_1_p14, i_j_out_1_p15, i_j_out_1_p16, nor_1_out,
       r_out_1_p11, r_out_1_p12, r_out_1_p13, r_out_1_p14, r_out_1_p15, r_out_1_p16;
  wire [3:0] i_j_out_1_p7, r_out_1_p7;

  nor nor_1 (nor_1_out, Op[0], Op[1], Op[2], Op[3], Op[4], Op[5]);
  // I___J_Out i_j_out_1: pin names not known; wires that end beside it: Op[0], Op[1], Op[2], Op[3], Op[4], Op[5], i_j_out_1_p7[0], i_j_out_1_p7[1], i_j_out_1_p7[2], i_j_out_1_p7[3], i_j_out_1_p11, i_j_out_1_p12, i_j_out_1_p13, i_j_out_1_p14, i_j_out_1_p15, i_j_out_1_p16, Extend[1], Extend[0]
  // R_Out r_out_1: pin names not known; wires that end beside it: Func[0], Func[1], Func[2], Func[3], Func[4], Func[5], r_out_1_p7[0], r_out_1_p7[1], r_out_1_p7[2], r_out_1_p7[3], r_out_1_p11, r_out_1_p12, r_out_1_p13, r_out_1_p14, r_out_1_p15, r_out_1_p16
  Multiplexer #(.width(4), .enable("false")) multiplexer_1 (
    .in0(i_j_out_1_p7), .in1(r_out_1_p7), .out(ALU_code), .sel(nor_1_out));
  Multiplexer #(.enable("false")) multiplexer_2 (.in0(i_j_out_1_p11), .in1(r_out_1_p11), .out(MUX1), .sel(nor_1_out));
  Multiplexer #(.enable("false")) multiplexer_3 (.in0(i_j_out_1_p12), .in1(r_out_1_p12), .out(MUX2), .sel(nor_1_out));
  Multiplexer #(.enable("false")) multiplexer_4 (.in0(i_j_out_1_p13), .in1(r_out_1_p13), .out(SAsel), .sel(nor_1_out));
  Multiplexer #(.enable("false")) multiplexer_5 (.in0(i_j_out_1_p14), .in1(r_out_1_p14), .out(Signed), .sel(nor_1_out));
  Multiplexer #(.enable("false")) multiplexer_6 (
    .in0(i_j_out_1_p15), .in1(r_out_1_p15), .out(WriteEnable1), .sel(nor_1_out));
  Multiplexer #(.enable("false")) multiplexer_7 (
    .in0(i_j_out_1_p16), .in1(r_out_1_p16), .out(WriteEnable2), .sel(nor_1_out));
endmodule

module I___J_Out (
  input  B0,
  input  B1,
  input  B2,
  input  B3,
  input  B4,
  input  B5,
  output O0,
  output O1,
  output O2,
  output O3,
  output MUX1,
  output MUX2,
  output SA,
  output Signed,
  output WE1,
  output WE2,
  output Extend,
  output SL,
  output L_S_Byte_or_Word,
  output Jump_Branch_Enable,
  output Link
);

  wire and_1_out, and_2_out, and_3_out, and_4_out, and_6_out, and_8_out, and_9_out, and_10_out, and_11_out,
       and_12_out, and_13_out, and_14_out, and_15_out, and_16_out, and_17_out, and_18_out, and_20_out,
       and_21_out, and_22_out, and_23_out, and_24_out, and_25_out, and_26_out, and_27_out, and_28_out,
       and_29_out, and_30_out, and_35_out, and_36_out, and_38_out, and_39_out, nand_1_out, nor_1_out,
       not_1_out, not_2_out, not_3_out, not_4_out, not_5_out, not_6_out, not_7_out, not_8_out, not_9_out,
       not_10_out, not_11_out, not_12_out, not_13_out, not_14_out, not_15_out, not_16_out, not_17_out,
       not_18_out, not_19_out, not_20_out, not_21_out, not_22_out, not_23_out, not_24_out, not_25_out,
       not_26_out, not_27_out, not_28_out, not_29_out, not_30_out, not_31_out, not_32_out, not_33_out,
       not_34_out, not_35_out, not_36_out, not_37_out, not_38_out, not_39_out, not_40_out, not_41_out,
       not_42_out, not_43_out, not_44_out, not_45_out, not_46_out, not_47_out, not_48_out, not_49_out,
       not_50_out, not_51_out, not_52_out, not_53_out, not_54_out, not_55_out, not_56_out, not_57_out,
       not_58_out, not_59_out, not_60_out, not_61_out, not_62_out, not_63_out, not_64_out, not_65_out,
       or_1_out, or_2_out, or_3_out, or_4_out, or_5_out, or_6_out, xnor_1_out, xnor_2_out, xnor_3_out,
       xnor_4_out, xnor_5_out;

  not not_1 (not_1_out, B5);
  not not_2 (not_2_out, B4);
  not not_3 (not_3_out, B2);
  not not_4 (not_4_out, B1);
  not not_5 (not_5_out, B2);
  not not_6 (not_6_out, B4);
  not not_7 (not_7_out, B2);
  not not_8 (not_8_out, B0);
  not not_9 (not_9_out, B2);
  not not_10 (not_10_out, B2);
  not not_11 (not_11_out, B1);
  not not_12 (not_12_out, B5);
  not not_13 (not_13_out, B4);
  and and_1 (and_1_out, B5, not_14_out, not_15_out);
  not not_14 (not_14_out, B4);
  not not_15 (not_15_out, B3);
  not not_16 (not_16_out, B1);
  and and_2 (and_2_out, B2, not_16_out, not_17_out);
  not not_17 (not_17_out, B0);
  not not_18 (not_18_out, B2);
  not not_19 (not_19_out, B5);
  not not_20 (not_20_out, B4);
  not not_21 (not_21_out, B2);
  not not_22 (not_22_out, B0);
  not not_23 (not_23_out, B4);
  not not_24 (not_24_out, B2);
  not not_25 (not_25_out, B5);
  not not_26 (not_26_out, B4);
  not not_27 (not_27_out, B2);
  not not_28 (not_28_out, B1);
  not not_29 (not_29_out, B0);
  and and_3 (and_3_out, B5, not_30_out, not_31_out);
  not not_30 (not_30_out, B4);
  not not_31 (not_31_out, B3);
  and and_4 (and_4_out, B2, not_32_out, not_33_out);
  not not_32 (not_32_out, B1);
  not not_33 (not_33_out, B0);
  not not_34 (not_34_out, B2);
  not not_35 (not_35_out, B4);
  not not_36 (not_36_out, B2);
  not not_37 (not_37_out, B2);
  not not_38 (not_38_out, B1);
  not not_39 (not_39_out, B2);
  not not_40 (not_40_out, B5);
  not not_41 (not_41_out, B4);
  not not_42 (not_42_out, B3);
  not not_43 (not_43_out, B2);
  not not_44 (not_44_out, B5);
  not not_45 (not_45_out, B4);
  not not_46 (not_46_out, B4);
  not not_47 (not_47_out, B2);
  not not_48 (not_48_out, B1);
  not not_49 (not_49_out, B0);
  not not_50 (not_50_out, B5);
  and and_5 (Jump_Branch_Enable, not_50_out, not_51_out, not_52_out);
  not not_51 (not_51_out, B4);
  not not_52 (not_52_out, B3);
  not not_53 (not_53_out, B2);
  and and_6 (and_6_out, not_53_out, B1, B0);
  and and_7 (O0, not_1_out, not_2_out, B3, not_3_out, B1);
  and and_8 (and_8_out, not_4_out, B0);
  and and_9 (and_9_out, not_5_out, B1);
  and and_10 (and_10_out, B2, B1, B0);
  and and_11 (and_11_out, B5, not_6_out);
  and and_12 (and_12_out, and_11_out, and_13_out);
  and and_13 (and_13_out, not_7_out, xnor_1_out);
  xnor xnor_1 (xnor_1_out, B1, B0);
  not not_54 (not_54_out, B4);
  not not_55 (not_55_out, B3);
  and and_14 (and_14_out, B5, not_54_out, not_55_out, B2, not_56_out, not_57_out);
  not not_56 (not_56_out, B1);
  not not_57 (not_57_out, B0);
  and and_15 (and_15_out, B2, B1, not_8_out);
  and and_16 (and_16_out, not_9_out, B1);
  and and_17 (and_17_out, not_10_out, not_11_out, B0);
  and and_18 (and_18_out, B2, B1, B0);
  and and_19 (MUX1, not_12_out, not_13_out, B3);
  or or_1 (or_1_out, and_2_out, and_20_out);
  and and_20 (and_20_out, not_18_out, xnor_2_out);
  xnor xnor_2 (xnor_2_out, B1, B0);
  and and_21 (and_21_out, not_19_out, not_20_out, B3, not_21_out, B1, not_22_out);
  and and_22 (and_22_out, B5, not_23_out);
  and and_23 (and_23_out, and_22_out, and_24_out);
  and and_24 (and_24_out, not_24_out, xnor_3_out);
  xnor xnor_3 (xnor_3_out, B1, B0);
  and and_25 (and_25_out, not_25_out, not_26_out, B3);
  nand nand_1 (nand_1_out, not_27_out, not_28_out, not_29_out);
  or or_2 (or_2_out, and_4_out, and_26_out);
  and and_26 (and_26_out, not_34_out, xnor_4_out);
  xnor xnor_4 (xnor_4_out, B1, B0);
  xnor xnor_5 (xnor_5_out, B1, B0);
  not not_58 (not_58_out, B5);
  not not_59 (not_59_out, B4);
  and and_27 (and_27_out, not_58_out, not_59_out, B3);
  and and_28 (and_28_out, not_37_out, not_38_out, B0);
  or or_3 (or_3_out, and_28_out, and_29_out);
  and and_29 (and_29_out, not_39_out, B1);
  and and_30 (and_30_out, not_40_out, not_41_out, not_42_out, not_43_out, B1);
  and and_31 (SL, not_44_out, not_45_out, B3, B2, B1, B0);
  and and_32 (L_S_Byte_or_Word, B5, not_46_out, not_47_out, not_48_out, not_49_out);
  and and_33 (Link, Jump_Branch_Enable, and_6_out);
  not not_60 (not_60_out, B5);
  not not_61 (not_61_out, B4);
  or or_4 (or_4_out, and_8_out, and_9_out, and_10_out);
  or or_5 (or_5_out, and_12_out, and_14_out);
  not not_62 (not_62_out, B5);
  not not_63 (not_63_out, B4);
  or or_6 (or_6_out, and_15_out, and_16_out);
  not not_64 (not_64_out, B5);
  not not_65 (not_65_out, B4);
  nor nor_1 (nor_1_out, and_17_out, and_18_out);
  and and_34 (MUX2, and_1_out, or_1_out);
  and and_35 (and_35_out, and_25_out, nand_1_out);
  and and_36 (and_36_out, and_3_out, or_2_out);
  and and_37 (WE2, B5, not_35_out, B3, not_36_out, xnor_5_out);
  and and_38 (and_38_out, and_27_out, or_3_out);
  and and_39 (and_39_out, not_60_out, not_61_out, B3, or_4_out);
  or or_7 (O1, and_39_out, or_5_out);
  and and_40 (O2, not_62_out, not_63_out, B3, or_6_out);
  and and_41 (O3, not_64_out, not_65_out, B3, nor_1_out);
  or or_8 (Signed, and_21_out, and_23_out);
  or or_9 (WE1, and_35_out, and_36_out);
  or or_10 (Extend, and_38_out, and_30_out);

  assign SA = 1'b1;
endmodule

module R_Out (
  input  B0,
  input  B1,
  input  B2,
  input  B3,
  input  B4,
  input  B5,
  output O0,
  output O1,
  output O2,
  output O3,
  output MUX1,
  output MUX2,
  output SA,
  output Signed,
  output WE1,
  output WE2,
  output Jump_Branch_Enable,
  output Link
);

  wire and_1_out, and_2_out, and_3_out, and_4_out, and_5_out, and_6_out, and_7_out, and_8_out, and_9_out,
       and_10_out, and_11_out, and_12_out, and_14_out, and_15_out, and_16_out, and_17_out, and_18_out,
       and_22_out, and_23_out, and_24_out, and_25_out, and_26_out, nand_1_out, nand_2_out, not_1_out,
       not_2_out, not_3_out, not_4_out, not_5_out, not_6_out, not_7_out, not_8_out, not_9_out, not_10_out,
       not_11_out, not_12_out, not_13_out, not_14_out, not_15_out, not_16_out, not_17_out, not_18_out,
       not_19_out, not_20_out, not_21_out, not_22_out, not_23_out, not_24_out, not_25_out, not_26_out,
       not_27_out, not_28_out, not_29_out, not_30_out, not_31_out, not_32_out, not_33_out, not_34_out,
       not_35_out, not_36_out, not_37_out, not_38_out, not_39_out, not_40_out, not_41_out, not_42_out,
       not_43_out, not_44_out, not_45_out, not_46_out, not_47_out, not_48_out, not_49_out, not_50_out,
       not_51_out, or_1_out, or_3_out, or_4_out;

  not not_1 (not_1_out, B4);
  not not_2 (not_2_out, B2);
  not not_3 (not_3_out, B5);
  not not_4 (not_4_out, B4);
  not not_5 (not_5_out, B2);
  not not_6 (not_6_out, B5);
  not not_7 (not_7_out, B4);
  not not_8 (not_8_out, B3);
  not not_9 (not_9_out, B2);
  not not_10 (not_10_out, B1);
  not not_11 (not_11_out, B2);
  not not_12 (not_12_out, B1);
  not not_13 (not_13_out, B2);
  not not_14 (not_14_out, B4);
  not not_15 (not_15_out, B3);
  not not_16 (not_16_out, B4);
  not not_17 (not_17_out, B2);
  not not_18 (not_18_out, B1);
  not not_19 (not_19_out, B4);
  not not_20 (not_20_out, B2);
  not not_21 (not_21_out, B0);
  not not_22 (not_22_out, B4);
  not not_23 (not_23_out, B2);
  not not_24 (not_24_out, B4);
  not not_25 (not_25_out, B3);
  not not_26 (not_26_out, B5);
  not not_27 (not_27_out, B4);
  not not_28 (not_28_out, B3);
  not not_29 (not_29_out, B1);
  not not_30 (not_30_out, B5);
  not not_31 (not_31_out, B4);
  not not_32 (not_32_out, B2);
  not not_33 (not_33_out, B1);
  and and_1 (and_1_out, B5, not_1_out, B3, not_2_out, B1);
  and and_2 (and_2_out, not_3_out, not_4_out, B3, not_5_out, B1);
  and and_3 (and_3_out, not_6_out, not_7_out, not_8_out, B1, B0);
  and and_4 (and_4_out, not_9_out, not_10_out, B0);
  and and_5 (and_5_out, not_11_out, B1, B0);
  and and_6 (and_6_out, B2, not_12_out, B0);
  and and_7 (and_7_out, B2, B1, B0);
  not not_34 (not_34_out, B5);
  and and_8 (and_8_out, not_34_out, not_35_out);
  not not_35 (not_35_out, B0);
  and and_9 (and_9_out, not_13_out, B1, B0);
  and and_10 (and_10_out, B2, B1);
  and and_11 (and_11_out, B5, not_14_out, not_15_out, B2);
  and and_12 (and_12_out, not_16_out, B3, not_17_out, B1);
  not not_36 (not_36_out, B5);
  not not_37 (not_37_out, B4);
  not not_38 (not_38_out, B3);
  nand nand_1 (nand_1_out, not_18_out, B0);
  and and_13 (Signed, B5, not_19_out, B3, not_20_out, B1, not_21_out);
  and and_14 (and_14_out, not_22_out, B3, not_23_out, B1);
  and and_15 (and_15_out, B5, not_24_out, not_25_out);
  and and_16 (and_16_out, and_15_out, or_1_out);
  or or_1 (or_1_out, B2, B0);
  and and_17 (and_17_out, not_26_out, not_27_out, not_28_out);
  and and_18 (and_18_out, and_17_out, nand_2_out);
  nand nand_2 (nand_2_out, not_29_out, B0);
  and and_19 (Jump_Branch_Enable, not_30_out, not_31_out, B3, not_32_out, not_33_out);
  not not_39 (not_39_out, B0);
  or or_2 (O0, and_1_out, and_2_out, and_3_out);
  not not_40 (not_40_out, B4);
  not not_41 (not_41_out, B3);
  or or_3 (or_3_out, and_4_out, and_5_out, and_6_out, and_7_out);
  not not_42 (not_42_out, and_8_out);
  not not_43 (not_43_out, B4);
  not not_44 (not_44_out, B2);
  not not_45 (not_45_out, B4);
  not not_46 (not_46_out, B3);
  or or_4 (or_4_out, and_9_out, and_10_out);
  not not_47 (not_47_out, B4);
  not not_48 (not_48_out, B2);
  not not_49 (not_49_out, B5);
  not not_50 (not_50_out, B4);
  not not_51 (not_51_out, B3);
  or or_5 (O3, and_11_out, and_12_out);
  and and_20 (SA, not_36_out, not_37_out, not_38_out, B2, nand_1_out);
  and and_21 (Link, Jump_Branch_Enable, not_39_out);
  and and_22 (and_22_out, B5, not_40_out, not_41_out, or_3_out);
  and and_23 (and_23_out, not_42_out, not_43_out, B3, not_44_out, B1);
  and and_24 (and_24_out, B5, not_45_out, not_46_out, or_4_out);
  and and_25 (and_25_out, B5, not_47_out, B3, not_48_out, B1);
  and and_26 (and_26_out, not_49_out, not_50_out, not_51_out, B1);
  or or_6 (O1, and_22_out, and_23_out);
  or or_7 (O2, and_24_out, and_25_out, and_26_out);
  or or_8 (WE1, and_14_out, and_16_out, and_18_out);

  assign MUX1 = 1'b0;
  assign MUX2 = 1'b0;
  assign WE2 = 1'b0;
endmodule

module SAVar (
  input  [4:0] SA_in,
  input  [31:0] A_in,
  input  Select,
  output [4:0] SA_out
);

  Multiplexer #(.width(5)) multiplexer_1 (.in0(SA_in), .in1(A_in[4:0]), .out(SA_out), .sel(Select));  // open: en
endmodule

module BitExtend (
  input  [15:0] Imm_In,
  input  [1:0] BitEx,
  output [31:0] Imm_Out
);

  wire multiplexer_1_out;
  wire [31:0] bit_extender_1_out;

  Multiplexer #(.enable("false")) multiplexer_1 (.in0(1'b0), .in1(Imm_In[15]), .out(multiplexer_1_out), .sel(BitEx[1]));
  assign bit_extender_1_out = {{16{multiplexer_1_out}}, Imm_In};  // Bit_Extender bit_extender_1
  Multiplexer #(.width(32), .enable("false")) multiplexer_2 (
    .in0(bit_extender_1_out), .in1({Imm_In, {16{1'b0}}}), .out(Imm_Out), .sel(BitEx[0]));
endmodule

module Execute (
  input  [3:0] ALUcode,
  input  [31:0] Out2,
  input  WEin,
  input  [31:0] Out1,
  input  [4:0] SA,
  input  [4:0] rd2,
  input  [4:0] rd1,
  input  WE2,
  input  [4:0] rt,
  input  [4:0] rs,
  input  WE1,
  input  [31:0] B,
  input  [31:0] A,
  input  [31:0] Immediate,
  input  ImmMux,
  input  Signed,
  output WER_out,
  output [31:0] C_out
);

  wire and_2_out, and_3_out, comparator_1_lt, comparator_2_lt, multiplexer_2_out, nand_1_out, not_1_out,
       not_2_out, not_3_out;
  wire [31:0] and_1_out, bit_extender_1_out, bit_extender_2_out, forward_1_forwarded, forward_2_forwarded,
       mips_alu_1_p5, multiplexer_1_out, multiplexer_3_out;

  Forward forward_1 (
    .Out2(Out2), .rd2(rd2), .WE1(WE1), .rd1(rd1), .Out1(Out1), .WE2(WE2), .rs(rt), .Out0(B),
    .Forwarded(forward_1_forwarded));
  Multiplexer #(.width(32), .enable("false")) multiplexer_1 (
    .in0(forward_1_forwarded), .in1(Immediate), .out(multiplexer_1_out), .sel(ImmMux));
  Forward forward_2 (
    .Out2(Out2), .rd2(rd2), .WE1(WE1), .rd1(rd1), .Out1(Out1), .WE2(WE2), .rs(rs), .Out0(A),
    .Forwarded(forward_2_forwarded));
  not not_1 (not_1_out, ALUcode[2]);
  assign and_1_out = bit_extender_1_out & forward_2_forwarded;  // AND_Gate and_1, 32 bits wide
  Comparator #(.width(32), .mode("unsigned")) comparator_1 (
    .a(forward_2_forwarded), .b(multiplexer_1_out), .lt(comparator_1_lt));  // open: gt, eq
  Comparator #(.width(32)) comparator_2 (
    .a(forward_2_forwarded), .b(multiplexer_1_out), .lt(comparator_2_lt));  // open: gt, eq
  and and_2 (and_2_out, ALUcode[0], ALUcode[1], ALUcode[2], ALUcode[3]);
  and and_3 (and_3_out, ALUcode[0], not_1_out, ALUcode[3]);
  // Mips_ALU mips_alu_1: pin names not known; wires that end beside it: and_1_out, multiplexer_1_out, ALUcode, SA, mips_alu_1_p5
  Multiplexer multiplexer_2 (
    .in0(comparator_1_lt), .in1(comparator_2_lt), .out(multiplexer_2_out), .sel(Signed));  // open: en
  nand nand_1 (nand_1_out, and_3_out, not_2_out);
  not not_2 (not_2_out, mips_alu_1_p5[0]);
  assign bit_extender_1_out = {{31{not_3_out}}, not_3_out};  // Bit_Extender bit_extender_1
  not not_3 (not_3_out, and_3_out);
  Multiplexer #(.width(32), .enable("false")) multiplexer_3 (
    .in0(mips_alu_1_p5), .in1(forward_2_forwarded), .out(multiplexer_3_out), .sel(and_3_out));
  assign bit_extender_2_out = {{31{1'b0}}, multiplexer_2_out};  // Bit_Extender bit_extender_2
  and and_4 (WER_out, nand_1_out, WEin);
  Multiplexer #(.width(32)) multiplexer_4 (
    .in0(multiplexer_3_out), .in1(bit_extender_2_out), .out(C_out), .sel(and_2_out));  // open: en
endmodule
