// Logisim project decode.circ as structural Verilog
module I___J_Out (
  input  B0,
  input  B1,
  input  B2,
  input  B3,
  input  B4,
  input  B5,
  output O0,
  output O1,
  output O2,
  output O3,
  output MUX1,
  output MUX2,
  output SA,
  output Signed,
  output WE1,
  output WE2,
  output Extend,
  output SL
);

  wire and_2_out, and_3_out, and_4_out, and_5_out, and_6_out, and_7_out, and_8_out, and_11_out, and_12_out,
       and_13_out, nor_1_out, not_1_out, not_2_out, not_3_out, not_4_out, not_5_out, not_6_out, not_7_out,
       not_8_out, not_9_out, not_10_out, not_11_out, not_12_out, not_13_out, not_14_out, not_15_out,
       not_16_out, not_17_out, not_18_out, not_19_out, not_20_out, not_21_out, not_22_out, not_23_out,
       not_24_out, not_25_out, not_26_out, not_27_out, not_28_out, or_1_out, or_2_out, or_3_out;

  not not_1 (not_1_out, B5);
  not not_2 (not_2_out, B4);
  not not_3 (not_3_out, B2);
  not not_4 (not_4_out, B1);
  not not_5 (not_5_out, B2);
  not not_6 (not_6_out, B0);
  not not_7 (not_7_out, B2);
  not not_8 (not_8_out, B2);
  not not_9 (not_9_out, B1);
  not not_10 (not_10_out, B5);
  not not_11 (not_11_out, B4);
  not not_12 (not_12_out, B5);
  not not_13 (not_13_out, B4);
  not not_14 (not_14_out, B2);
  not not_15 (not_15_out, B0);
  not not_16 (not_16_out, B2);
  not not_17 (not_17_out, B1);
  not not_18 (not_18_out, B2);
  not not_19 (not_19_out, B5);
  not not_20 (not_20_out, B4);
  and and_1 (O0, not_1_out, not_2_out, B3, not_3_out, B1);
  and and_2 (and_2_out, not_4_out, B0);
  and and_3 (and_3_out, not_5_out, B1);
  and and_4 (and_4_out, B2, B1, B0);
  and and_5 (and_5_out, B2, B1, not_6_out);
  and and_6 (and_6_out, not_7_out, B1);
  and and_7 (and_7_out, not_8_out, not_9_out, B0);
  and and_8 (and_8_out, B2, B1, B0);
  and and_9 (MUX1, not_10_out, not_11_out, B3);
  and and_10 (Signed, not_12_out, not_13_out, B3, not_14_out, B1, not_15_out);
  not not_21 (not_21_out, B5);
  and and_11 (and_11_out, not_21_out, not_22_out, B3);
  not not_22 (not_22_out, B4);
  and and_12 (and_12_out, not_16_out, not_17_out, B0);
  or or_1 (or_1_out, and_12_out, and_13_out);
  and and_13 (and_13_out, not_18_out, B1);
  and and_14 (SL, not_19_out, not_20_out, B3, B2, B1, B0);
  not not_23 (not_23_out, B5);
  not not_24 (not_24_out, B4);
  or or_2 (or_2_out, and_2_out, and_3_out, and_4_out);
  not not_25 (not_25_out, B5);
  not not_26 (not_26_out, B4);
  or or_3 (or_3_out, and_5_out, and_6_out);
  not not_27 (not_27_out, B5);
  not not_28 (not_28_out, B4);
  nor nor_1 (nor_1_out, and_7_out, and_8_out);
  and and_15 (Extend, and_11_out, or_1_out);
  and and_16 (O1, not_23_out, not_24_out, B3, or_2_out);
  and and_17 (O2, not_25_out, not_26_out, B3, or_3_out);
  and and_18 (O3, not_27_out, not_28_out, B3, nor_1_out);

  assign MUX2 = 1'b0;
  assign SA = 1'b1;
  assign WE1 = 1'b1;
  assign WE2 = 1'b0;
endmodule

module R_Out (
  input  B0,
  input  B1,
  input  B2,
  input  B3,
  input  B4,
  input  B5,
  output O0,
  output O1,
  output O2,
  output O3,
  output MUX1,
  output MUX2,
  output SA,
  output Signed,
  output WE1,
  output WE2,
  output Extend,
  output SL
);

  wire and_1_out, and_2_out, and_3_out, and_4_out, and_5_out, and_6_out, and_7_out, and_8_out, and_9_out,
       and_10_out, and_11_out, and_12_out, and_15_out, and_16_out, and_17_out, and_18_out, and_19_out,
       nand_1_out, not_1_out, not_2_out, not_3_out, not_4_out, not_5_out, not_6_out, not_7_out, not_8_out,
       not_9_out, not_10_out, not_11_out, not_12_out, not_13_out, not_14_out, not_15_out, not_16_out,
       not_17_out, not_18_out, not_19_out, not_20_out, not_21_out, not_22_out, not_23_out, not_24_out,
       not_25_out, not_26_out, not_27_out, not_28_out, not_29_out, not_30_out, not_31_out, not_32_out,
       not_33_out, not_34_out, not_35_out, not_36_out, not_37_out, not_38_out, or_2_out, or_3_out;

  not not_1 (not_1_out, B4);
  not not_2 (not_2_out, B2);
  not not_3 (not_3_out, B5);
  not not_4 (not_4_out, B4);
  not not_5 (not_5_out, B2);
  not not_6 (not_6_out, B5);
  not not_7 (not_7_out, B4);
  not not_8 (not_8_out, B3);
  not not_9 (not_9_out, B2);
  not not_10 (not_10_out, B1);
  not not_11 (not_11_out, B2);
  not not_12 (not_12_out, B1);
  not not_13 (not_13_out, B2);
  not not_14 (not_14_out, B4);
  not not_15 (not_15_out, B3);
  not not_16 (not_16_out, B4);
  not not_17 (not_17_out, B2);
  not not_18 (not_18_out, B1);
  not not_19 (not_19_out, B4);
  not not_20 (not_20_out, B2);
  not not_21 (not_21_out, B0);
  and and_1 (and_1_out, B5, not_1_out, B3, not_2_out, B1);
  and and_2 (and_2_out, not_3_out, not_4_out, B3, not_5_out, B1);
  and and_3 (and_3_out, not_6_out, not_7_out, not_8_out, B1, B0);
  and and_4 (and_4_out, not_9_out, not_10_out, B0);
  and and_5 (and_5_out, not_11_out, B1, B0);
  and and_6 (and_6_out, B2, not_12_out, B0);
  and and_7 (and_7_out, B2, B1, B0);
  not not_22 (not_22_out, B5);
  and and_8 (and_8_out, not_22_out, not_23_out);
  not not_23 (not_23_out, B0);
  and and_9 (and_9_out, not_13_out, B1, B0);
  and and_10 (and_10_out, B2, B1);
  and and_11 (and_11_out, B5, not_14_out, not_15_out, B2);
  and and_12 (and_12_out, not_16_out, B3, not_17_out, B1);
  not not_24 (not_24_out, B5);
  not not_25 (not_25_out, B4);
  not not_26 (not_26_out, B3);
  nand nand_1 (nand_1_out, not_18_out, B0);
  and and_13 (Signed, B5, not_19_out, B3, not_20_out, B1, not_21_out);
  or or_1 (O0, and_1_out, and_2_out, and_3_out);
  not not_27 (not_27_out, B4);
  not not_28 (not_28_out, B3);
  or or_2 (or_2_out, and_4_out, and_5_out, and_6_out, and_7_out);
  not not_29 (not_29_out, and_8_out);
  not not_30 (not_30_out, B4);
  not not_31 (not_31_out, B2);
  not not_32 (not_32_out, B4);
  not not_33 (not_33_out, B3);
  or or_3 (or_3_out, and_9_out, and_10_out);
  not not_34 (not_34_out, B4);
  not not_35 (not_35_out, B2);
  not not_36 (not_36_out, B5);
  not not_37 (not_37_out, B4);
  not not_38 (not_38_out, B3);
  or or_4 (O3, and_11_out, and_12_out);
  and and_14 (SA, not_24_out, not_25_out, not_26_out, B2, nand_1_out);
  and and_15 (and_15_out, B5, not_27_out, not_28_out, or_2_out);
  and and_16 (and_16_out, not_29_out, not_30_out, B3, not_31_out, B1);
  and and_17 (and_17_out, B5, not_32_out, not_33_out, or_3_out);
  and and_18 (and_18_out, B5, not_34_out, B3, not_35_out, B1);
  and and_19 (and_19_out, not_36_out, not_37_out, not_38_out, B1);
  or or_5 (O1, and_15_out, and_16_out);
  or or_6 (O2, and_17_out, and_18_out, and_19_out);

  assign Extend = 1'b0;
  assign MUX1 = 1'b0;
  assign MUX2 = 1'b0;
  assign SL = 1'b0;
  assign WE1 = 1'b1;
  assign WE2 = 1'b0;
endmodule

module De (
  input  [5:0] Op,
  input  [5:0] Func,
  output [3:0] ALU_code,
  output MUX1,
  output MUX2,
  output ShiftAmt,
  output Signed,
  output WriteEnable1,
  output WriteEnable2,
  output Extend,
  output SL
);

  wire i_j_out_1_extend, i_j_out_1_mux1, i_j_out_1_mux2, i_j_out_1_sa, i_j_out_1_signed, i_j_out_1_sl,
       i_j_out_1_we1, i_j_out_1_we2, nor_1_out, r_out_1_extend, r_out_1_mux1, r_out_1_mux2, r_out_1_sa,
       r_out_1_signed, r_out_1_sl, r_out_1_we1, r_out_1_we2;
  wire [3:0] i_j_out_1_o0, r_out_1_o0;

  nor nor_1 (nor_1_out, Op[0], Op[1], Op[2], Op[3], Op[4], Op[5]);
  I___J_Out i_j_out_1 (
    .B0(Op[0]), .B1(Op[1]), .B2(Op[2]), .B3(Op[3]), .B4(Op[4]), .B5(Op[5]), .O0(i_j_out_1_o0[0]),
    .O1(i_j_out_1_o0[1]), .O2(i_j_out_1_o0[2]), .O3(i_j_out_1_o0[3]), .MUX1(i_j_out_1_mux1),
    .MUX2(i_j_out_1_mux2), .SA(i_j_out_1_sa), .Signed(i_j_out_1_signed), .WE1(i_j_out_1_we1),
    .WE2(i_j_out_1_we2), .Extend(i_j_out_1_extend), .SL(i_j_out_1_sl));
  R_Out r_out_1 (
    .B0(Func[0]), .B1(Func[1]), .B2(Func[2]), .B3(Func[3]), .B4(Func[4]), .B5(Func[5]), .O0(r_out_1_o0[0]),
    .O1(r_out_1_o0[1]), .O2(r_out_1_o0[2]), .O3(r_out_1_o0[3]), .MUX1(r_out_1_mux1), .MUX2(r_out_1_mux2),
    .SA(r_out_1_sa), .Signed(r_out_1_signed), .WE1(r_out_1_we1), .WE2(r_out_1_we2), .Extend(r_out_1_extend),
    .SL(r_out_1_sl));
  Multiplexer #(.width(4), .enable("false")) multiplexer_1 (
    .in0(i_j_out_1_o0), .in1(r_out_1_o0), .out(ALU_code), .sel(nor_1_out));
  Multiplexer #(.enable("false")) multiplexer_2 (.in0(i_j_out_1_mux1), .in1(r_out_1_mux1), .out(MUX1), .sel(nor_1_out));
  Multiplexer #(.enable("false")) multiplexer_3 (.in0(i_j_out_1_mux2), .in1(r_out_1_mux2), .out(MUX2), .sel(nor_1_out));
  Multiplexer #(.enable("false")) multiplexer_4 (.in0(i_j_out_1_sa), .in1(r_out_1_sa), .out(ShiftAmt), .sel(nor_1_out));
  Multiplexer #(.enable("false")) multiplexer_5 (
    .in0(i_j_out_1_signed), .in1(r_out_1_signed), .out(Signed), .sel(nor_1_out));
  Multiplexer #(.enable("false")) multiplexer_6 (
    .in0(i_j_out_1_we1), .in1(r_out_1_we1), .out(WriteEnable1), .sel(nor_1_out));
  Multiplexer #(.enable("false")) multiplexer_7 (
    .in0(i_j_out_1_we2), .in1(r_out_1_we2), .out(WriteEnable2), .sel(nor_1_out));
  Multiplexer #(.enable("false")) multiplexer_8 (
    .in0(i_j_out_1_extend), .in1(r_out_1_extend), .out(Extend), .sel(nor_1_out));
  Multiplexer #(.enable("false")) multiplexer_9 (.in0(i_j_out_1_sl), .in1(r_out_1_sl), .out(SL), .sel(nor_1_out));
endmodule
